# Fritzing sketch wemos-wifi-robot (saved by Fritzing 0.9.4)
breadboards: 1

parts:
  L298N1 = L298N DC motor driver
  WeMos_D1_Mini1 = WeMos D1 Mini

nets:
  N1: L298N1.GND, WeMos_D1_Mini1.G
  5V: L298N1.5V, WeMos_D1_Mini1.5V
  N2: L298N1.ENA, WeMos_D1_Mini1.D3
  N3: L298N1.ENB, WeMos_D1_Mini1.D8
  N4: L298N1.IN1, WeMos_D1_Mini1.D2
  N5: L298N1.IN2, WeMos_D1_Mini1.D1
  N6: L298N1.IN3, WeMos_D1_Mini1.D7
  N7: L298N1.IN4, WeMos_D1_Mini1.D6

custom parts:
  L298N DC motor driver: 2x DC motor driver with 78M05 positive voltage regulator (7..35 V) L298N: max 46 V, 2 A Set 5 V Enable jumper to enable 5 V regultor (needed for the L298N) and +5 V output at screw terminal or supply external +5 V at screw terminal Set ENA and/or ENB to +5 V to enable motor permanently or supply ENA and/or ENB with PWM signal IN1 and IN2 set rotation directory for motor A (OUT1/OUT2) IN2 and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

// code stored in the sketch: Untitled.ino
//This example will use a static IP to control the switching of a relay. Over LAN using a web browser. 
//A lot of this code have been resued from the example on the ESP8266 Learning Webpage below. 
//http://www.esp8266learning.com/wemos-webserver-example.php


//CODE START 
#include <Arduino.h>
#include <ESP8266WiFi.h>


// WiFi network information
const char* ssid = "error_418_2.4";         // WiFi name (wemos will only connect to 2.4GHz network)
const char* password = "MuffinFightsFrogs"; // WiFi password


// Motor constants
const int ENB = D8;
const int IN3 = D6;
const int IN4 = D7;
const int ENA = D4;
const int IN1 = D3;
const int IN2 = D2;
const int PWMSpeed = 600;


// States
const int FORWARD = 0;
const int BACKWARD = 1;
const int STOP = 2;
const int LEFT = 3;
const int RIGHT = 4;
int state;



// Intervals
unsigned long turnStartTime;
unsigned long driveStartTime;
unsigned long driveIntervalTime = 1000; // default drive time
unsigned long turnIntervalTime = 175;   // default turn time
unsigned long previousMillis = 0;
unsigned long currentMillis = 0;


// Setting up the http server
WiFiServer server(81);
IPAddress ip(192, 168, 0, 99); // desired IP address on network
IPAddress gateway(192, 168, 1, 1); // set gateway to match network
IPAddress subnet(255, 255, 255, 0); // set subnet mask to match network



// void setup is where we initialize variables, pin modes, start using libraries, etc. 
//The setup function will only run once, after each powerup or reset of the wemos board.
void setup() {
  Serial.begin(115200);
  delay(10);


  initMotors();


  initWifi();


  initHTTP();
}


//void loop is where you put all your code. it is a funtion that returns nothing and will repeat over and over again
void loop() {
  // Check if a client has connected
  WiFiClient client = server.available();
  if (!client) {
    return;
  }
 
  // Wait until the client sends some data
  Serial.println("new client");
  while(!client.available()){
    delay(1);
  }
 
  // Read the first line of the request
  String request = client.readStringUntil('\r');
  Serial.println(request);
  client.flush();
 
  //Match the request, checking to see what the currect state is
  if (request.indexOf("/F") != -1) {
    state = mForward();
    Serial.println("state set forward");
  } else if (request.indexOf("/B") != -1){
    state = mBackward();
    delay(1000);
    mStop();
    Serial.println("state set backward");
  } else if (request.indexOf("/R") != -1){
    state = mRight();
    delay(turnIntervalTime);
    mStop();
    Serial.println("state set right");
  } else if (request.indexOf("/L") != -1){
    state = mLeft();
    delay(turnIntervalTime);
    mStop();
    Serial.println("state set left");
  } else if (request.indexOf("/S") != -1){
    state = mStop();
    Serial.println("state set stop");
  }


//



  
  // Return the response, build the html page
  //7
  client.println("HTTP/1.1 200 OK");
  client.println("Content-Type: text/html");
  client.println(""); //  do not forget this one
  client.println("<!DOCTYPE HTML>");
  client.println("<html>");
  client.println("<head><meta name=\"viewport\" content=\"width=device-width, initial-scale=1\">");
  client.println("<link rel=\"icon\" href=\"data:,\">");


  client.println("<br><br><br>");
  client.println("<a href=\"/F\">Click here for FORWARD.</a> <br><br><br>");
  client.println("<a href=\"/S\">Click here for STOP.</a> <br><br><br>");
  client.println("<a href=\"/B\">Click here for BACKWARD.</a><br><br><br>");
  client.println("<a href=\"/L\">Click here for LEFT.</a><br><br><br>");
  client.println("<a href=\"/R\">Click here for RIGHT.</a> <br><br><br>");
  client.println("</html>");
 
  delay(1);
  Serial.println("Client disconnected");
  Serial.println("");
 
}//END


//void stateIntervalHandler() {
//  currentMillis = millis();
//  if ((currentMillis - driveStartTime) > driveIntervalTime) {
//    state = mStop();
//    Serial.println("STOPSTOPSTOP");
//  }
//  if (currentMillis - turnStartTime > turnIntervalTime) {
//    state = mStop();
//  }
//  Serial.println("Turn time: " + currentMillis - turnStartTime);
//  Serial.println("Drive time: " + currentMillis - driveStartTime);
//}


void initMotors() {
  pinMode(ENA, OUTPUT);
  pinMode(ENB, OUTPUT);


  pinMode(IN1, OUTPUT);
  pinMode(IN2, OUTPUT);
  pinMode(IN3, OUTPUT);
  pinMode(IN4, OUTPUT);
  
  digitalWrite(IN1, LOW);
  digitalWrite(IN2, LOW);
  digitalWrite(IN3, LOW);
  digitalWrite(IN4, LOW);


  analogWrite(ENB, PWMSpeed);
  analogWrite(ENA, PWMSpeed);
}


int mForward() {
  digitalWrite(IN1, HIGH);
  digitalWrite(IN2, LOW);
  digitalWrite(IN3, HIGH);
  digitalWrite(IN4, LOW);
  driveStartTime = millis();
  return FORWARD;
}


int mBackward() {
  digitalWrite(IN1, LOW);
  digitalWrite(IN2, HIGH);
  digitalWrite(IN3, LOW);
  digitalWrite(IN4, HIGH);
  driveStartTime = millis();
  return BACKWARD;
}


int mStop() {
  digitalWrite(IN1, LOW);
  digitalWrite(IN2, LOW);
  digitalWrite(IN3, LOW);
  digitalWrite(IN4, LOW);
  return STOP;
}


int mLeft() {
  digitalWrite(IN1, LOW);
  digitalWrite(IN2, HIGH);
  digitalWrite(IN3, HIGH);
  digitalWrite(IN4, LOW);
  turnStartTime = millis();
  return LEFT;
}


int mRight() {
  digitalWrite(IN1, HIGH);
  digitalWrite(IN2, LOW);
  digitalWrite(IN3, LOW);
  digitalWrite(IN4, HIGH);
  turnStartTime = millis();
  return RIGHT;
}


void initWifi() {
    // assigned IP address
  Serial.print(F("Setting static ip to : "));
  Serial.println(ip);
  
  // Connect to WiFi network
  Serial.println();
  Serial.println();
  Serial.print("Connecting to ");
  Serial.println(ssid);
  WiFi.config(ip, gateway, subnet); 
  WiFi.begin(ssid, password);
  //Trying to connect it will display dots
  while (WiFi.status() != WL_CONNECTED) {
    delay(500);
    Serial.print(".");
  }
  Serial.println("");
  Serial.println("WiFi connected");
}


void initHTTP() {
    // Start the server
  server.begin();
  Serial.println("Server started");
 
  // Print the IP address
  Serial.print("Use this URL : ");
  Serial.print("http://");
  Serial.print(WiFi.localIP());
  Serial.println("/"); 
}
